// Logisim project arm_single_cycle.circ as structural Verilog: 29 circuits, main circuit main
module main (
  input  in_1,
  input  in_2,
  input  in_3,
  input  [1:0] Branch,
  input  in_5,
  input  in_6,
  input  [31:0] in_7,
  input  in_8,
  input  in_9,
  input  in_10,
  input  in_11,
  input  in_12,
  input  in_13,
  input  in_14,
  input  in_15,
  input  in_16,
  input  in_17,
  input  in_18,
  input  in_19,
  input  in_20,
  input  [3:0] in_21,
  input  [3:0] in_22,
  input  Z,
  input  N,
  input  V,
  input  [31:0] in_26,
  input  [31:0] A,
  input  [31:0] B,
  input  [1:0] in_29,
  input  [3:0] Cond,
  input  [3:0] in_31,
  output out_32,
  output out_33,
  output out_34,
  output out_35,
  output out_36,
  output out_37,
  output out_38,
  output out_39,
  output [31:0] out_40,
  output [3:0] out_41,
  output [31:0] out_42,
  output out_43,
  output out_44,
  output out_45,
  output out_46
);

  wire and_3_out, and_4_out, and_6_out, not_1_out, xnor_1_out;
  wire [31:0] rom_1_data;

  // Probe on A
  assign out_40 = in_7 & in_26;  // AND_Gate and_1, 32 bits wide
  and and_2 (out_32, in_1, in_2);
  // Probe on B
  Decoder #(.select(4)) decoder_1 (
    .out0(out_33), .out1(out_34), .out2(out_35), .out3(out_36), .out4(out_37), .out5(out_38), .sel(in_21));  // open: out6, out7, out8, out9, out10, out11, out12, out13, out14, out15, en
  ALU_conditional alu_conditional_1 (
    .ALU_Control(in_29), .r(out_42), .Zero(out_45), .ALU_FLAGS(out_41), .Negative(out_44), .Carry(out_43),
    .Overflow(out_46), .A(A), .B(B));
  // Probe on out_42
  // Probe on Branch[1]
  Multiplexer #(.select(4)) multiplexer_1 (
    .in0(in_3), .in1(in_5), .in2(in_6), .in3(in_8), .in4(in_9), .in5(in_10), .in6(in_11), .in7(in_12),
    .in8(in_13), .in9(in_14), .in10(in_15), .in11(in_16), .in12(in_17), .in13(in_18), .in14(in_19),
    .in15(in_20), .out(out_39), .sel(in_22));  // open: en
  ROM #(.addrWidth(4), .dataWidth(32)) rom_1 (.addr(in_31), .data(rom_1_data));  // open: sel
  and and_3 (and_3_out, 1'b1, Branch[0]);
  buf and_4 (and_4_out, ~Branch[1]);  // AND_Gate AND_Gate
  // AND_Gate and_5 has open pins: in0=and_3_out, in1=and_4_out, out=open
  xnor xnor_1 (xnor_1_out, N, V);
  not not_1 (not_1_out, Z);
  and and_6 (and_6_out, Z, xnor_1_out);
  Multiplexer #(.select(4)) multiplexer_2 (
    .in0(not_1_out), .in1(Z), .in12(and_6_out), .in14(1'b1), .sel(Cond));  // open: in2, in3, in4, in5, in6, in7, in8, in9, in10, in11, in13, in15, out, en

  // Notes on the sheet:
  //   Check branch inst in PC logic using 2-bit input
  //   eq
  //   ne
  //   gt
  //   uncond
endmodule

module ALU (
  input  [31:0] A,
  input  [31:0] B,
  input  [1:0] ALU_Control,
  output [31:0] r
);

  wire [31:0] adder_1_out, and_1_out, or_1_out, subtractor_1_out;

  // Probe on A
  // Probe on B
  Adder #(.width(32)) adder_1 (.a(A), .b(B), .out(adder_1_out));  // open: cin, cout
  Subtractor #(.width(32)) subtractor_1 (.a(A), .b(B), .out(subtractor_1_out));  // open: bin, bout
  assign or_1_out = A | B;  // OR_Gate or_1, 32 bits wide
  assign and_1_out = A & B;  // AND_Gate and_1, 32 bits wide
  Multiplexer #(.select(2), .width(32)) multiplexer_1 (
    .in0(adder_1_out), .in1(subtractor_1_out), .in2(or_1_out), .in3(and_1_out), .out(r), .sel(ALU_Control));  // open: en
  // Probe on r
endmodule

module data_memory (
  input  clk,
  input  we,
  input  RESET,
  input  [31:0] address,
  input  [31:0] wd,
  output [31:0] rd
);

  wire not_1_out;

  // Probe on address
  // Probe on address
  // Probe on address[9:2]
  not not_1 (not_1_out, we);
  // Probe on rd
  RAM #(.dataWidth(32), .bus("separate")) ram_1 (
    .addr(address[9:2]), .din(wd), .data(rd), .str(we), .sel(1'b1), .clk(clk), .ld(not_1_out), .clr(RESET));
endmodule

module instruction_memory (
  input  [31:0] addr,
  output [31:0] rd
);

  // Probe on addr
  // Probe on rd[11:0]
  // Probe on rd[15:12]
  // Probe on rd[19:16]
  // Probe on rd[20]
  ROM #(.dataWidth(32)) rom_1 (.addr(addr[9:2]), .data(rd), .sel(1'b1));
  // Probe on rd[25]
  // Probe on rd
  // Probe on rd[24:21]
  // Probe on rd[23:0]
  // Probe on rd[24]
  // Probe on rd[27:26]
  // Probe on rd[31:28]
  // Probe on rd[31:28]

  // Other names for the same wires on the sheet: imm24[23:0] = rd[23:0]; Op2[11:0] = rd[11:0]; rd_t[3:0] = rd[15:12];
  //   rn[3:0] = rd[19:16]; S = rd[20]; OP_CODE[3:0] = rd[24:21]; l_bit = rd[24]; I = rd[25]; type[1:0] = rd[27:26];
  //   COND[3:0] = rd[31:28]; cond_t[3:0] = rd[31:28]

  // Notes on the sheet:
  //   Extract word address
  //   contents of rom_1 (hex, n*v repeats v):
  //   e3a00014 e3a01002 e2412002 e2413001 e3a04000 e3500000 a000009 e3500001 a000007 e1510000 c1a00004
  //   ca000004 e0824003 e1a02003 e1a03004 e2811001 eafffff7 e12fff1e
endmodule

module register_file (
  input  [31:0] R15,
  input  we,
  input  [3:0] writeAddr,
  input  [31:0] writeData,
  input  clk,
  input  Reset,
  input  [3:0] A1,
  input  [3:0] A2,
  input  [3:0] get_reg_data,
  input  [3:0] get_reg_data_2,
  output [31:0] RD1,
  output [31:0] RD2,
  output [31:0] r14,
  output [31:0] out_14,
  output [31:0] reg_data
);

  wire decoder_1_out0, decoder_1_out1, decoder_1_out2, decoder_1_out3, decoder_1_out4, decoder_1_out5,
       decoder_1_out6, decoder_1_out7, decoder_1_out8, decoder_1_out9, decoder_1_out10, decoder_1_out11,
       decoder_1_out12, decoder_1_out13, decoder_1_out14;
  wire [31:0] R0_q, R1_q, R2_q, R3_q, R5_q, R6_q, R7_q, R8_q, R9_q, R10_q, R11_q, R12_q, R13_q, register_1_q;

  Decoder #(.select(4), .disabled(0)) decoder_1 (
    .out0(decoder_1_out0), .out1(decoder_1_out1), .out2(decoder_1_out2), .out3(decoder_1_out3),
    .out4(decoder_1_out4), .out5(decoder_1_out5), .out6(decoder_1_out6), .out7(decoder_1_out7),
    .out8(decoder_1_out8), .out9(decoder_1_out9), .out10(decoder_1_out10), .out11(decoder_1_out11),
    .out12(decoder_1_out12), .out13(decoder_1_out13), .out14(decoder_1_out14), .sel(writeAddr), .en(we));  // open: out15
  Register #(.width(32)) R0 (.D(writeData), .en(decoder_1_out0), .Q(R0_q), .clk(clk), .clr(Reset));
  Register #(.width(32)) R1 (.D(writeData), .en(decoder_1_out1), .Q(R1_q), .clk(clk), .clr(Reset));
  Register #(.width(32)) R2 (.D(writeData), .en(decoder_1_out2), .Q(R2_q), .clk(clk), .clr(Reset));
  Register #(.width(32)) R3 (.D(writeData), .en(decoder_1_out3), .Q(R3_q), .clk(clk), .clr(Reset));
  Register #(.width(32)) register_1 (.D(writeData), .en(decoder_1_out4), .Q(register_1_q), .clk(clk), .clr(Reset));
  Register #(.width(32)) R5 (.D(writeData), .en(decoder_1_out5), .Q(R5_q), .clk(clk), .clr(Reset));
  Register #(.width(32)) R6 (.D(writeData), .en(decoder_1_out6), .Q(R6_q), .clk(clk), .clr(Reset));
  Register #(.width(32)) R7 (.D(writeData), .en(decoder_1_out7), .Q(R7_q), .clk(clk), .clr(Reset));
  Register #(.width(32)) R8 (.D(writeData), .en(decoder_1_out8), .Q(R8_q), .clk(clk), .clr(Reset));
  Register #(.width(32)) R9 (.D(writeData), .en(decoder_1_out9), .Q(R9_q), .clk(clk), .clr(Reset));
  Register #(.width(32)) R10 (.D(writeData), .en(decoder_1_out10), .Q(R10_q), .clk(clk), .clr(Reset));
  Register #(.width(32)) R12 (.D(writeData), .en(decoder_1_out12), .Q(R12_q), .clk(clk), .clr(Reset));
  Register #(.width(32)) R11 (.D(writeData), .en(decoder_1_out11), .Q(R11_q), .clk(clk), .clr(Reset));
  Register #(.width(32)) R13 (.D(writeData), .en(decoder_1_out13), .Q(R13_q), .clk(clk), .clr(Reset));
  Register #(.width(32)) u_R14 (.D(writeData), .en(decoder_1_out14), .Q(r14), .clk(clk), .clr(Reset));
  Multiplexer #(.select(4), .width(32), .disabled(0)) multiplexer_1 (
    .in0(R0_q), .in1(R1_q), .in2(R2_q), .in3(R3_q), .in4(register_1_q), .in5(R5_q), .in6(R6_q), .in7(R7_q),
    .in8(R8_q), .in9(R9_q), .in10(R10_q), .in11(R11_q), .in12(R12_q), .in13(R13_q), .in14(r14), .in15(R15),
    .out(RD1), .sel(A1));  // open: en
  Multiplexer #(.select(4), .width(32), .disabled(0)) multiplexer_2 (
    .in0(R0_q), .in1(R1_q), .in2(R2_q), .in3(R3_q), .in4(register_1_q), .in5(R5_q), .in6(R6_q), .in7(R7_q),
    .in8(R8_q), .in9(R9_q), .in10(R10_q), .in11(R11_q), .in12(R12_q), .in13(R13_q), .in14(r14), .in15(R15),
    .out(RD2), .sel(A2));  // open: en
  Multiplexer #(.select(4), .width(32), .disabled(0)) multiplexer_3 (
    .in0(R0_q), .in1(R1_q), .in2(R2_q), .in3(R3_q), .in4(register_1_q), .in5(R5_q), .in6(R6_q), .in7(R7_q),
    .in8(R8_q), .in9(R9_q), .in10(R10_q), .in11(R11_q), .in12(R12_q), .in13(R13_q), .in14(r14), .in15(R15),
    .out(out_14), .sel(get_reg_data));  // open: en
  Multiplexer #(.select(4), .width(32), .disabled(0)) multiplexer_4 (
    .in0(R0_q), .in1(R1_q), .in2(R2_q), .in3(R3_q), .in4(register_1_q), .in5(R5_q), .in6(R6_q), .in7(R7_q),
    .in8(R8_q), .in9(R9_q), .in10(R10_q), .in11(R11_q), .in12(R12_q), .in13(R13_q), .in14(r14), .in15(R15),
    .out(reg_data), .sel(get_reg_data_2));  // open: en

  // Notes on the sheet:
  //   A1,A2,-> one of 16 registers as src operands
  //   write port takes 4-bit address input A3; 32-bit write data input WD3; Write enable input WE3; and clock
  //   if the write enable is asserted, reg file writes data into specified reg on rising edge of clock
  //   a read of r15 returns the value from PC + 8 and writes to r15 must be specifically handled to update the pc bc it is separate from reg file
  //   RD1, RD2 -> take A1 and A2
  //   reads 32-bit reg vals of A1, and A2 onto RD1 and RD2
endmodule

module cpu (
  input  RESET,
  input  [3:0] reg1,
  output [31:0] out_3,
  output [31:0] reg1_data
);

  wire and_2_out, bx, clock_1_out, control_1_alusrc, control_1_memtoreg, control_1_memwrite, control_1_pcsrc,
       control_1_regwrite, isNeg, LINK, mov, REG_SRC;
  wire [1:0] control_1_alucontrol, control_1_immsrc;
  wire [1:1] control_1_regsrc;
  wire [3:0] alu_conditional_1_alu_flags, multiplexer_2_out, multiplexer_3_out, multiplexer_4_out,
       multiplexer_5_out;
  wire [31:0] adder_1_out, adder_2_out, data_memory_1_rd, extend_1_extimm, instruction_memory_1_rd,
       multiplexer_1_out, multiplexer_6_out, multiplexer_7_out, multiplexer_9_out, multiplexer_10_out, PC,
       r14, RD1, register_file_1_rd2, SRC_2, undriven;

  // Probe on clock_1_out
  // Probe on multiplexer_1_out
  // Probe on control_1_pcsrc
  // Probe on multiplexer_1_out
  Multiplexer #(.width(32), .disabled(0)) multiplexer_1 (
    .in0(adder_1_out), .in1(multiplexer_10_out), .out(multiplexer_1_out), .sel(control_1_pcsrc));  // open: en
  // Probe on instruction_memory_1_rd[27:4]
  // Probe on instruction_memory_1_rd[15:12]
  // Probe on PC
  // Probe on PC
  Register #(.width(32)) u_PC (.D(multiplexer_1_out), .Q(PC), .clk(clock_1_out), .clr(RESET));  // open: en
  // Probe on instruction_memory_1_rd[27:4]
  // Probe on instruction_memory_1_rd[27:26]
  // Probe on instruction_memory_1_rd[25:20]
  // Probe on instruction_memory_1_rd[15:12]
  // Probe on instruction_memory_1_rd[25:20]
  // Probe on instruction_memory_1_rd[15:12]
  // Probe on instruction_memory_1_rd
  Adder #(.width(32)) adder_1 (.a(PC), .b(32'h4), .out(adder_1_out), .cin(1'b0));  // open: cout
  // Probe on instruction_memory_1_rd[31:28]
  // Probe on instruction_memory_1_rd[31:28]
  instruction_memory instruction_memory_1 (.addr(PC), .rd(instruction_memory_1_rd));
  // Probe on alu_conditional_1_alu_flags
  // Probe on instruction_memory_1_rd[19:16]
  // Probe on instruction_memory_1_rd[3:0]
  Adder #(.width(32)) adder_2 (.a(32'h4), .b(adder_1_out), .out(adder_2_out), .cin(1'b0));  // open: cout
  // Probe on instruction_memory_1_rd[23:0]
  // Probe on instruction_memory_1_rd[23:0]
  Clock clock_1 (.out(clock_1_out));
  Multiplexer #(.width(4), .disabled(0)) multiplexer_2 (
    .in0(instruction_memory_1_rd[19:16]), .in1(4'b1111), .out(multiplexer_2_out), .sel(REG_SRC));  // open: en
  Multiplexer #(.width(4), .disabled(0)) multiplexer_3 (
    .in0(instruction_memory_1_rd[3:0]), .in1(instruction_memory_1_rd[15:12]), .out(multiplexer_3_out),
    .sel(control_1_regsrc[1]));  // open: en
  // Probe on instruction_memory_1_rd[15:12]
  // Probe on adder_2_out
  control control_1 (
    .Cond_3_0(instruction_memory_1_rd[31:28]), .ALUFlags3_0(alu_conditional_1_alu_flags),
    .Op(instruction_memory_1_rd[27:26]), .Funct(instruction_memory_1_rd[25:20]),
    .Rd(instruction_memory_1_rd[15:12]), .PCSrc(control_1_pcsrc), .RegWrite(control_1_regwrite),
    .MemWrite(control_1_memwrite), .MemtoReg(control_1_memtoreg), .ALUSrc(control_1_alusrc),
    .ImmSrc(control_1_immsrc), .RegSrc({control_1_regsrc[1], REG_SRC}), .ALUControl(control_1_alucontrol),
    .clk(clock_1_out), .in4_27(instruction_memory_1_rd[27:4]), .bx(bx), .link(LINK), .mov(mov));
  // Probe on multiplexer_3_out
  Multiplexer #(.width(4), .disabled(0)) multiplexer_4 (
    .in0(multiplexer_2_out), .in1(4'b1110), .out(multiplexer_4_out), .sel(bx));  // open: en
  // Probe on multiplexer_10_out
  // Probe on multiplexer_4_out
  Multiplexer #(.width(4), .disabled(0)) multiplexer_5 (
    .in0(instruction_memory_1_rd[15:12]), .in1(4'b1110), .out(multiplexer_5_out), .sel(LINK));  // open: en
  // Probe on multiplexer_6_out
  Extend extend_1 (
    .ExtImm(extend_1_extimm), ._24bits(instruction_memory_1_rd[23:0]), .ImmSrc(control_1_immsrc),
    .isNeg(isNeg));
  // Probe on r14
  // Probe on control_1_alusrc
  // Probe on multiplexer_5_out
  Multiplexer #(.width(32), .disabled(0)) multiplexer_6 (
    .in0(multiplexer_10_out), .in1(adder_1_out), .out(multiplexer_6_out), .sel(LINK));  // open: en
  // Probe on multiplexer_6_out
  register_file register_file_1 (
    .R15(adder_2_out), .we(control_1_regwrite), .writeAddr(multiplexer_5_out), .writeData(multiplexer_6_out),
    .clk(clock_1_out), .Reset(RESET), .RD1(RD1), .A1(multiplexer_4_out), .RD2(register_file_1_rd2),
    .A2(multiplexer_3_out), .get_reg_data(reg1), .out_14(reg1_data), .r14(r14));  // open: get_reg_data_2, reg_data
  // Probe on reg1_data
  // Probe on control_1_immsrc
  // Probe on RD1
  // Probe on RD1
  // Probe on register_file_1_rd2
  // AND_Gate and_1 has open pins: in0=REG_SRC, in1=bx, out=open
  // Probe on SRC_2
  and and_2 (and_2_out, isNeg, ~LINK);  // AND_Gate
  Multiplexer #(.width(32), .disabled(0)) multiplexer_7 (
    .in0(undriven), .in1(PC), .out(multiplexer_7_out), .sel(and_2_out));  // open: en
  Multiplexer #(.width(32), .disabled(0)) multiplexer_8 (
    .in0(register_file_1_rd2), .in1(extend_1_extimm), .out(SRC_2), .sel(control_1_alusrc));  // open: en
  // Probe on extend_1_extimm
  // Probe on extend_1_extimm
  // Probe on control_1_alucontrol
  // Probe on out_3
  ALU_conditional alu_conditional_1 (
    .ALU_Control(control_1_alucontrol), .r(out_3), .ALU_FLAGS(alu_conditional_1_alu_flags), .A(RD1), .B(SRC_2));  // open: Zero, Negative, Carry, Overflow
  // Probe on control_1_alucontrol
  // Probe on out_3
  data_memory data_memory_1 (
    .address(out_3), .wd(register_file_1_rd2), .we(control_1_memwrite), .RESET(RESET), .rd(data_memory_1_rd),
    .clk(clock_1_out));
  special_exec special_exec_1 (
    .src2(SRC_2), .ALUResult(out_3), .RD1(RD1), .link(LINK), .regSrc(REG_SRC), .bx(bx), .mov(mov));  // open: result
  Multiplexer #(.width(32), .disabled(0)) multiplexer_9 (
    .in0(out_3), .in1(SRC_2), .out(multiplexer_9_out), .sel(mov));  // open: en
  // Probe on multiplexer_9_out
  // Probe on data_memory_1_rd
  Multiplexer #(.width(32), .disabled(0)) multiplexer_10 (
    .in0(multiplexer_9_out), .in1(data_memory_1_rd), .out(multiplexer_10_out), .sel(control_1_memtoreg));  // open: en
  // Probe on multiplexer_10_out

  // Notes on the sheet:
  //   PCsrc
  //   PC'
  //   PC
  //   inst about to be executed
  //   PC Plus 4
  //   CVZN
  //   NOTE: LEFTSHIFT YOUR IMMEDIATE BEFORE SIGN EXTENDING FOR BRANCH
  //   RegSrc
  //   PC plus 8
  //   regWrite
  //   ALUSrc
  //   ALUControl
  //   ALUResult
  //   checks special execution: mov and bx
  //   MemWrite
  //   ReadData
  //   MemToReg
  //   Result
endmodule

module special_exec (
  input  link,
  input  regSrc,
  input  bx,
  input  mov,
  input  [31:0] src2,
  input  [31:0] ALUResult,
  input  [31:0] RD1,
  output [31:0] result
);

  wire spec_out;
  wire [3:1] branch_out;
  wire [31:0] adder_1_out, adder_3_out, multiplexer_1_out, subtractor_1_out, undriven;

  and bl (branch_out[3], link, regSrc);
  Adder #(.width(32)) adder_1 (.a(undriven), .b(32'h8), .out(adder_1_out), .cin(1'b0));  // open: cout
  Adder #(.width(32)) adder_2 (.a(RD1), .b(32'h8), .cin(1'b0));  // open: out, cout
  and branch (branch_out[1], ~link, regSrc);  // AND_Gate
  Multiplexer #(.select(4), .width(32)) multiplexer_1 (
    .in1(src2), .in2(ALUResult), .in4(RD1), .in8(ALUResult), .out(multiplexer_1_out),
    .sel({branch_out[3], bx, branch_out[1], mov}), .en(spec_out));  // open: in0, in3, in5, in6, in7, in9, in10, in11, in12, in13, in14, in15
  or spec (spec_out, branch_out[3], bx, branch_out[1], mov);
  Multiplexer #(.width(32)) multiplexer_2 (
    .in0(ALUResult), .in1(multiplexer_1_out), .out(result), .sel(spec_out));  // open: en
  Subtractor #(.width(32)) subtractor_1 (.a(RD1), .b(32'h8), .out(subtractor_1_out));  // open: bin, bout
  // Probe on result
  Adder #(.width(32)) adder_3 (.a(src2), .b(subtractor_1_out), .out(adder_3_out), .cin(1'b0));  // open: cout
  // Probe on adder_3_out

  // Notes on the sheet:
  //   mov
  //   branch
  //   bx lr
  //   bl
endmodule

module ALU_conditional (
  input  [31:0] A,
  input  [31:0] B,
  input  [1:0] ALU_Control,
  output [31:0] r,
  output Zero,
  output [3:0] ALU_FLAGS,
  output Negative,
  output Carry,
  output Overflow
);

  wire adder_1_cout;
  wire [31:0] adder_1_out, and_1_out, or_1_out, subtractor_1_out;

  // Probe on A
  // Probe on A
  // Probe on B
  Adder #(.width(32)) adder_1 (.a(A), .b(B), .out(adder_1_out), .cout(adder_1_cout));  // open: cin
  Subtractor #(.width(32)) subtractor_1 (.a(A), .b(B), .out(subtractor_1_out));  // open: bin, bout
  assign or_1_out = A | B;  // OR_Gate or_1, 32 bits wide
  assign and_1_out = A & B;  // AND_Gate and_1, 32 bits wide
  Multiplexer #(.select(2), .width(32)) multiplexer_1 (
    .in0(adder_1_out), .in1(subtractor_1_out), .in2(and_1_out), .in3(or_1_out),
    .out({ALU_FLAGS[3], r[30:0]}), .sel(ALU_Control));  // open: en
  conditional conditional_1 (
    .ALUControl(ALU_Control), .carry(ALU_FLAGS[1]), .Overflow(ALU_FLAGS[0]), .A(A[31]), .B(B[31]),
    .C_out(adder_1_cout));
  // Probe on {ALU_FLAGS[3], r[30:0]}
  and and_2 (ALU_FLAGS[2], ~r[0], ~r[1], ~r[2], ~r[3], ~r[4], ~r[5], ~r[6], ~r[7], ~r[8], ~r[9], ~r[10], ~r[11], ~r[12], ~r[13], ~r[14], ~r[15], ~r[16], ~r[17], ~r[18], ~r[19], ~r[20], ~r[21], ~r[22], ~r[23], ~r[24], ~r[25], ~r[26], ~r[27], ~r[28], ~r[29], ~r[30], ~ALU_FLAGS[3]);  // AND_Gate

  assign Carry = ALU_FLAGS[1];
  assign Negative = ALU_FLAGS[3];
  assign Overflow = ALU_FLAGS[0];
  assign r[31] = ALU_FLAGS[3];
  assign Zero = ALU_FLAGS[2];

  // Notes on the sheet:
  //   NCZV
endmodule

module conditional (
  input  A,
  input  B,
  input  C_out,
  input  [1:0] ALUControl,
  output carry,
  output Overflow
);

  wire adder_1_out, not_1_out, xnor_1_out, xor_1_out;

  Adder #(.width(1)) adder_1 (.a(A), .b(B), .out(adder_1_out));  // open: cin, cout
  // Probe on adder_1_out
  not not_1 (not_1_out, ALUControl[1]);
  xor xor_1 (xor_1_out, adder_1_out, A);
  NotExactlyOne xnor_1 (.out(xnor_1_out), .in0(B), .in1(A), .in2(ALUControl[0]));
  and and_1 (carry, C_out, not_1_out);
  and and_2 (Overflow, not_1_out, xor_1_out, xnor_1_out);

  // Notes on the sheet:
  //   carry
  //   overflow
endmodule

module control (
  input  clk,
  input  [3:0] Cond_3_0,
  input  [3:0] ALUFlags3_0,
  input  [1:0] Op,
  input  [5:0] Funct,
  input  [3:0] Rd,
  input  [23:0] in4_27,
  output PCSrc,
  output RegWrite,
  output MemWrite,
  output MemtoReg,
  output ALUSrc,
  output [1:0] ImmSrc,
  output [1:0] RegSrc,
  output [1:0] ALUControl,
  output bx,
  output link,
  output mov
);

  wire bx_comparator_1_out_2, MEM_W, N_WRITE, PCS, REG_W;
  wire [1:0] FLAG_W;

  // Probe on in4_27
  // Probe on Cond_3_0
  // Probe on ALUFlags3_0
  // Probe on Op
  // Probe on Funct
  bx_comparator bx_comparator_1 (.in24(in4_27), .out_2(bx_comparator_1_out_2));
  // Probe on Rd
  decoder decoder_1 (
    .RD(Rd), .Op(Op), .Funct_5_0(Funct), .PCS(PCS), .RegWrite(REG_W), .MemWrite(MEM_W), .MemToReg(MemtoReg),
    .ALUSrc(ALUSrc), .ImmSrc(ImmSrc), .RegSrc(RegSrc), .ALUControl(ALUControl), .FlagW(FLAG_W),
    .NoWrite(N_WRITE), .is_bx(bx_comparator_1_out_2), .bx(bx), .link(link), .mov(mov));
  // Probe on FLAG_W
  // Probe on REG_W
  // Probe on PCS
  // Probe on MEM_W
  conditional_logic conditional_logic_1 (
    .PCS(PCS), .RegW(REG_W), .MemW(MEM_W), .FlagW(FLAG_W), .Cond(Cond_3_0), .PCSrc(PCSrc),
    .RegWrite(RegWrite), .MemWrite(MemWrite), .ALUFlags(ALUFlags3_0), .clk(clk), .NoWrite(N_WRITE));
  // Probe on N_WRITE
endmodule

module main_decoder (
  input  [1:0] Op,
  input  is_bx,
  input  [5:0] Func,
  output RegWrite,
  output ALUOp,
  output MemWrite,
  output MemtoReg,
  output ALUSrc,
  output [1:0] ImmSrc,
  output [1:0] RegSrc,
  output Branch,
  output bx,
  output Link,
  output mov
);

  wire and_1_out, and_2_out, and_3_out, and_4_out, and_5_out, and_6_out, B_Link_out, not_1_out, not_2_out,
       not_3_out, not_4_out, or_1_out;

  // Probe on Op[1]
  not not_1 (not_1_out, Op[1]);
  // Probe on Op[0]
  not not_2 (not_2_out, Op[0]);
  not not_3 (not_3_out, Func[5]);
  not not_4 (not_4_out, Func[0]);
  and and_1 (and_1_out, not_1_out, ~is_bx, not_2_out, not_3_out);  // AND_Gate
  and and_2 (and_2_out, not_1_out, ~is_bx, not_2_out, Func[5]);  // AND_Gate
  and and_3 (and_3_out, not_1_out, ~is_bx, Op[0], not_4_out);  // AND_Gate
  and and_4 (and_4_out, not_1_out, ~is_bx, Op[0], Func[0]);  // AND_Gate
  and and_5 (and_5_out, Op[1], ~is_bx, not_2_out);  // AND_Gate
  and and_6 (and_6_out, is_bx, not_2_out, not_1_out);
  and B_Link (B_Link_out, and_5_out, Func[4]);
  main_decoder_output main_decoder_output_1 (
    .RegWrite(RegWrite), .ALUOp(ALUOp), .MemWrite(MemWrite), .MemtoReg(MemtoReg), .ALUSrc(ALUSrc),
    .ImmSrc(ImmSrc), .RegSrc(RegSrc), .Branch_2(Branch), .DP_Reg(and_1_out), .DP_Imm(and_2_out),
    .str(and_3_out), .ldr(and_4_out), .Branch(and_5_out), .Bx(and_6_out), .bx_2(bx), .Link(B_Link_out),
    .Link_2(Link));
  or or_1 (or_1_out, and_1_out, and_2_out);
  and and_7 (mov, or_1_out, Func[1], ~Func[2], Func[3], Func[4]);  // AND_Gate

  // Notes on the sheet:
  //   1
  //   0
  //   1
  //   0
  //   1
  //   0
  //   1
  //   0
  //   DPreg
  //   DPImm
  //   str
  //   ldr
  //   branch
  //   bx
endmodule

module Extend (
  input  [23:0] _24bits,
  input  [1:0] ImmSrc,
  output [31:0] ExtImm,
  output isNeg
);

  wire [31:0] n8bit_extend_1_out_2, n12bit_extend_1_out_2, n24bit_extend_1_out_2, shifter_1_out;

  _8bit_extend u_8bit_extend_1 (.out_2(n8bit_extend_1_out_2), .in_1(_24bits));
  _12bit_extend u_12bit_extend_1 (.out_2(n12bit_extend_1_out_2), .in_1(_24bits));
  _24bit_extend u_24bit_extend_1 (.out_2(n24bit_extend_1_out_2), .in_1(_24bits), .isNeg(isNeg));
  Shifter #(.width(32)) shifter_1 (.in(n24bit_extend_1_out_2), .\dist (5'b00010), .out(shifter_1_out));
  Multiplexer #(.select(2), .width(32)) multiplexer_1 (
    .in0(n8bit_extend_1_out_2), .in1(n12bit_extend_1_out_2), .in2(shifter_1_out), .out(ExtImm), .sel(ImmSrc));  // open: in3, en
  // Probe on shifter_1_out
endmodule

module _8bit_extend (
  input  [23:0] in_1,
  output [31:0] out_2
);

  assign out_2 = {{24{1'b0}}, in_1[7:0]};  // Bit_Extender bit_extender_1
endmodule

module _12bit_extend (
  input  [23:0] in_1,
  output [31:0] out_2
);

  assign out_2 = {{20{1'b0}}, in_1[11:0]};  // Bit_Extender bit_extender_1
endmodule

module _24bit_extend (
  input  [23:0] in_1,
  output [31:0] out_2,
  output isNeg
);

  wire [23:0] shifter_1_out;
  wire [31:0] adder_1_out, bit_extender_1_out, multiplexer_1_out, subtractor_1_out;

  // Probe on in_1
  Shifter #(.width(24)) shifter_1 (.in(in_1), .\dist (5'b00010), .out(shifter_1_out));
  // Probe on shifter_1_out
  assign bit_extender_1_out = {{8{shifter_1_out[23]}}, shifter_1_out};  // Bit_Extender bit_extender_1
  // Probe on bit_extender_1_out
  // Probe on {{9{in_1[23]}}, in_1[22:0]}
  Subtractor #(.width(32)) subtractor_1 (
    .a({{9{in_1[23]}}, in_1[22:0]}), .b(32'h8), .out(subtractor_1_out));  // open: bin, bout
  Adder #(.width(32)) adder_1 (.a({{9{in_1[23]}}, in_1[22:0]}), .b(32'h8), .out(adder_1_out));  // open: cin, cout
  Multiplexer #(.width(32)) multiplexer_1 (
    .in0(subtractor_1_out), .in1(adder_1_out), .out(multiplexer_1_out), .sel(in_1[23]));  // open: en

  assign isNeg = in_1[23];
  assign out_2 = {{9{in_1[23]}}, in_1[22:0]};

  // Other names for the same wires on the sheet: SIGN_BIT = in_1[23]
endmodule

module conditional_logic (
  input  PCS,
  input  RegW,
  input  NoWrite,
  input  MemW,
  input  [1:0] FlagW,
  input  [3:0] Cond,
  input  [3:0] ALUFlags,
  input  clk,
  output PCSrc,
  output RegWrite,
  output MemWrite
);

  wire cond_check_1_condex;
  wire [1:0] and_1_out, bit_extender_1_out, register_1_q, register_2_q;

  Register #(.width(2)) register_1 (.D(ALUFlags[3:2]), .en(and_1_out[0]), .Q(register_1_q), .clk(clk));  // open: clr
  Register #(.width(2)) register_2 (.D(ALUFlags[1:0]), .en(and_1_out[1]), .Q(register_2_q), .clk(clk));  // open: clr
  // Probe on and_1_out
  // Probe on register_2_q
  // Probe on register_1_q
  // Probe on bit_extender_1_out
  assign and_1_out = FlagW & bit_extender_1_out;  // AND_Gate and_1, 2 bits wide
  assign bit_extender_1_out = {{1{cond_check_1_condex}}, cond_check_1_condex};  // Bit_Extender bit_extender_1
  cond_check cond_check_1 (.Flags3_2(register_1_q), .Flags1_0(register_2_q), .CondEx(cond_check_1_condex), .Cond(Cond));
  and and_2 (PCSrc, PCS, cond_check_1_condex);
  and and_3 (RegWrite, RegW, ~NoWrite, cond_check_1_condex);  // AND_Gate
  and and_4 (MemWrite, MemW, cond_check_1_condex);
  // Probe on cond_check_1_condex

  // Notes on the sheet:
  //   CondEx
endmodule

module decoder (
  input  [3:0] RD,
  input  [1:0] Op,
  input  [5:0] Funct_5_0,
  input  is_bx,
  output PCS,
  output RegWrite,
  output MemWrite,
  output MemToReg,
  output ALUSrc,
  output [1:0] ImmSrc,
  output [1:0] RegSrc,
  output bx,
  output link,
  output mov,
  output [1:0] ALUControl,
  output NoWrite,
  output [1:0] FlagW
);

  wire main_decoder_1_aluop, main_decoder_1_branch;

  // Probe on Funct_5_0[4:0]
  // Probe on Funct_5_0[4:0]
  PC_logic pc_logic_1 (.Rd_3_0(RD), .RegWrite(RegWrite), .PCS(PCS), .Branch(main_decoder_1_branch));  // open: bx
  main_decoder main_decoder_1 (
    .Op(Op), .Func(Funct_5_0), .RegWrite(RegWrite), .ALUOp(main_decoder_1_aluop), .MemWrite(MemWrite),
    .MemtoReg(MemToReg), .ALUSrc(ALUSrc), .ImmSrc(ImmSrc), .RegSrc(RegSrc), .Branch(main_decoder_1_branch),
    .is_bx(is_bx), .bx(bx), .Link(link), .mov(mov));
  ALU_decoder ALUOp (
    .Funct(Funct_5_0[4:0]), .ALUControl(ALUControl), .FlagW(FlagW), .ALUOp(main_decoder_1_aluop),
    .NoWrite(NoWrite), .branch(main_decoder_1_branch));

  // Notes on the sheet:
  //   ALUOp
  //   FlagW0 = 1 ->CV(Flags1:0) are saved 
  //   FlagW1  = 1 -> NZ(Flags3:2) are saved
endmodule

module ALU_decoder (
  input  ALUOp,
  input  branch,
  input  [4:0] Funct,
  output [1:0] ALUControl,
  output NoWrite,
  output [1:0] FlagW
);

  wire [1:0] set_control_1_alucontrol;

  // Probe on Funct
  // Probe on Funct
  // Probe on Funct[4:1]
  // Probe on Funct[0]
  set_Control set_control_1 (
    .ALUControl(set_control_1_alucontrol), .FlagW(FlagW), .funct4_0(Funct[4:1]), .Funct0(Funct[0]),
    .NoWrite(NoWrite), .in_3(branch));
  Multiplexer #(.width(2), .disabled(0)) multiplexer_1 (
    .in0(2'b00), .in1(set_control_1_alucontrol), .out(ALUControl), .sel(ALUOp));  // open: en
  Multiplexer #(.width(2)) multiplexer_2 (.in0(ALUControl), .in1(2'b01), .out(ALUControl));  // open: sel, en
endmodule

module PC_logic (
  input  [3:0] Rd_3_0,
  input  RegWrite,
  input  bx,
  input  Branch,
  output PCS
);

  wire and_1_out, and_2_out, and_3_out, and_4_out;

  and and_1 (and_1_out, Rd_3_0[0], Rd_3_0[1], Rd_3_0[2], Rd_3_0[3]);
  and and_2 (and_2_out, and_1_out, 1'b1);
  and and_3 (and_3_out, RegWrite, 1'b1);
  // Probe on and_2_out
  // Probe on and_3_out
  and and_4 (and_4_out, and_2_out, and_3_out);
  or or_1 (PCS, and_4_out, Branch);
endmodule

module set_Control (
  input  [3:0] funct4_0,
  input  Funct0,
  input  in_3,
  output NoWrite,
  output [1:0] ALUControl,
  output [1:0] FlagW
);

  wire and_1_out;
  wire [1:0] get_flagw_1_flagw;

  Multiplexer #(.select(4), .width(2), .disabled(0)) multiplexer_1 (
    .in0(2'b10), .in2(2'b01), .in4(2'b00), .in5(2'b00), .in9(2'b11), .in10(2'b01), .in12(2'b11),
    .in13(2'b11), .out(ALUControl), .sel(funct4_0));  // open: in1, in3, in6, in7, in8, in11, in14, in15, en
  // Probe on funct4_0
  get_FlagW get_flagw_1 (.FlagW(get_flagw_1_flagw), .ALUControl1(ALUControl));  // open: in_2
  Multiplexer #(.select(4), .disabled(0)) multiplexer_2 (
    .in0(1'b0), .in1(1'b0), .in2(1'b0), .in3(1'b0), .in4(1'b0), .in5(1'b0), .in6(1'b0), .in7(1'b0),
    .in8(1'b0), .in9(1'b0), .in10(1'b1), .in11(1'b0), .in12(1'b0), .in13(1'b0), .in14(1'b0), .in15(1'b0),
    .out(NoWrite), .sel(funct4_0));  // open: en
  and and_1 (and_1_out, Funct0, ~in_3);  // AND_Gate
  Multiplexer #(.width(2), .disabled(0)) multiplexer_3 (
    .in0(2'b00), .in1(get_flagw_1_flagw), .out(FlagW), .sel(and_1_out));  // open: en
endmodule

module get_FlagW (
  input  [1:0] ALUControl1,
  input  in_2,
  output [1:0] FlagW
);

  wire and_1_out, not_1_out;

  and and_1 (and_1_out, ALUControl1[1], 1'b1);
  not not_1 (not_1_out, and_1_out);
  and and_2 (FlagW[1], ~in_2, 1'b1);  // AND_Gate
  and and_3 (FlagW[0], not_1_out, ~in_2);  // AND_Gate
endmodule

module main_decoder_output (
  input  DP_Reg,
  input  DP_Imm,
  input  str,
  input  ldr,
  input  Branch,
  input  Bx,
  input  Link,
  output RegWrite,
  output ALUOp,
  output MemWrite,
  output MemtoReg,
  output ALUSrc,
  output [1:0] ImmSrc,
  output [1:0] RegSrc,
  output Link_2,
  output Branch_2,
  output bx_2
);

  or or_1 (RegWrite, DP_Reg, ldr, Link, Bx, DP_Imm);
  or or_2 (ALUOp, DP_Reg, DP_Imm);
  or or_3 (ALUSrc, DP_Imm, str, Link, ldr, Branch);
  and and_1 (bx_2, ~Branch, ~ldr, ~str, ~Link, ~DP_Imm, ~DP_Reg, Bx);  // AND_Gate
  or or_4 (RegSrc[0], Branch, Link, Bx);
  or or_5 (ImmSrc[0], str, ldr);
  nor nor_1 (ImmSrc[1], DP_Imm, str, ldr);

  assign Branch_2 = Branch;
  assign Link_2 = Link;
  assign MemtoReg = ldr;
  assign MemWrite = str;
  assign RegSrc[1] = str;
endmodule

module cond_check (
  input  [1:0] Flags3_2,
  input  [3:0] Cond,
  input  [1:0] Flags1_0,
  output CondEx
);

  wire and_1_out, and_2_out, not_1_out, not_2_out, xor_1_out;

  xor xor_1 (xor_1_out, Flags3_2[1], Flags1_0[0]);
  and and_1 (and_1_out, Flags3_2[0], not_1_out);
  not not_1 (not_1_out, xor_1_out);
  not not_2 (not_2_out, Flags3_2[0]);
  Multiplexer #(.select(4)) multiplexer_1 (
    .in0(Flags3_2[0]), .in1(not_2_out), .in12(and_1_out), .in14(1'b1), .out(CondEx), .sel(Cond));  // open: in2, in3, in4, in5, in6, in7, in8, in9, in10, in11, in13, in15, en
  // AND_Gate and_2 has open pins: out=and_2_out
  // OR_Gate or_1 has open pins: in0=and_2_out, out=open

  // Notes on the sheet:
  //   Z
  //   N
  //   V
  //   C
  //   eq
  //   ne
  //   gt
endmodule

module registers (
  input  [31:0] R15,
  input  we,
  input  [3:0] writeAddr,
  input  [31:0] writeData,
  input  clk,
  input  Reset,
  input  [3:0] A1,
  input  [3:0] A2,
  output [31:0] RD1,
  output [31:0] RD2
);

  wire decoder_1_out0, decoder_1_out1, decoder_1_out2, decoder_1_out3, decoder_1_out4, decoder_1_out5,
       decoder_1_out6, decoder_1_out7, decoder_1_out8, decoder_1_out9, decoder_1_out10, decoder_1_out11,
       decoder_1_out12, decoder_1_out13, decoder_1_out14;
  wire [31:0] R0_q, R1_q, R2_q, R3_q, R5_q, R6_q, R7_q, R8_q, R9_q, R10_q, R11_q, R12_q, R13_q, R14_q,
       register_1_q;

  Decoder #(.select(4)) decoder_1 (
    .out0(decoder_1_out0), .out1(decoder_1_out1), .out2(decoder_1_out2), .out3(decoder_1_out3),
    .out4(decoder_1_out4), .out5(decoder_1_out5), .out6(decoder_1_out6), .out7(decoder_1_out7),
    .out8(decoder_1_out8), .out9(decoder_1_out9), .out10(decoder_1_out10), .out11(decoder_1_out11),
    .out12(decoder_1_out12), .out13(decoder_1_out13), .out14(decoder_1_out14), .sel(writeAddr), .en(we));  // open: out15
  Register #(.width(32)) R0 (.D(writeData), .en(decoder_1_out0), .Q(R0_q), .clk(clk), .clr(Reset));
  Register #(.width(32)) R1 (.D(writeData), .en(decoder_1_out1), .Q(R1_q), .clk(clk), .clr(Reset));
  Register #(.width(32)) R2 (.D(writeData), .en(decoder_1_out2), .Q(R2_q), .clk(clk), .clr(Reset));
  Register #(.width(32)) register_1 (.D(writeData), .en(decoder_1_out4), .Q(register_1_q), .clk(clk), .clr(Reset));
  Register #(.width(32)) R3 (.D(writeData), .en(decoder_1_out3), .Q(R3_q), .clk(clk), .clr(Reset));
  Register #(.width(32)) R5 (.D(writeData), .en(decoder_1_out5), .Q(R5_q), .clk(clk), .clr(Reset));
  Register #(.width(32)) R6 (.D(writeData), .en(decoder_1_out6), .Q(R6_q), .clk(clk), .clr(Reset));
  Register #(.width(32)) R7 (.D(writeData), .en(decoder_1_out7), .Q(R7_q), .clk(clk), .clr(Reset));
  Register #(.width(32)) R8 (.D(writeData), .en(decoder_1_out8), .Q(R8_q), .clk(clk), .clr(Reset));
  Register #(.width(32)) R9 (.D(writeData), .en(decoder_1_out9), .Q(R9_q), .clk(clk), .clr(Reset));
  Register #(.width(32)) R10 (.D(writeData), .en(decoder_1_out10), .Q(R10_q), .clk(clk), .clr(Reset));
  Register #(.width(32)) R11 (.D(writeData), .en(decoder_1_out11), .Q(R11_q), .clk(clk), .clr(Reset));
  Register #(.width(32)) R12 (.D(writeData), .en(decoder_1_out12), .Q(R12_q), .clk(clk), .clr(Reset));
  Register #(.width(32)) R13 (.D(writeData), .en(decoder_1_out13), .Q(R13_q), .clk(clk), .clr(Reset));
  Register #(.width(32)) R14 (.D(writeData), .en(decoder_1_out14), .Q(R14_q), .clk(clk), .clr(Reset));
  Multiplexer #(.select(4), .width(32)) multiplexer_1 (
    .in0(R0_q), .in1(R1_q), .in2(R2_q), .in3(R3_q), .in4(register_1_q), .in5(R5_q), .in6(R6_q), .in7(R7_q),
    .in8(R8_q), .in9(R9_q), .in10(R10_q), .in11(R11_q), .in12(R12_q), .in13(R13_q), .in14(R14_q), .in15(R15),
    .out(RD1), .sel(A1));  // open: en
  Multiplexer #(.select(4), .width(32)) multiplexer_2 (
    .in0(R0_q), .in1(R1_q), .in2(R2_q), .in3(R3_q), .in4(register_1_q), .in5(R5_q), .in6(R6_q), .in7(R7_q),
    .in8(R8_q), .in9(R9_q), .in10(R10_q), .in11(R11_q), .in12(R12_q), .in13(R13_q), .in14(R14_q), .in15(R15),
    .out(RD2), .sel(A2));  // open: en
endmodule

module ALU_dec2 (
  input  ALUOp,
  input  Funct4,
  input  Funct3,
  input  Funct2,
  input  Funct1,
  input  Funct0,
  output [1:0] ALUcontrol,
  output [1:0] FlagW
);

  wire and_1_out, and_2_out;

  and and_1 (and_1_out, ALUOp, Funct4, ~Funct3, Funct2, ~Funct1, Funct0);  // AND_Gate
  and and_2 (and_2_out, ALUOp, ~Funct4, Funct3, ~Funct2, ~Funct1, Funct0);  // AND_Gate
  or or_1 (FlagW[0], and_1_out, and_2_out);

  assign ALUcontrol = 2'b00;
  assign FlagW[1] = 1'b0;
endmodule

module bx_comparator (
  input  [23:0] in24,
  output out_2
);

  wire [23:0] xnor_1_out;

  assign xnor_1_out = ~(in24 ^ 24'h12fff1);  // XNOR_Gate xnor_1, 24 bits wide
  and and_1 (out_2, xnor_1_out[0], xnor_1_out[1], xnor_1_out[2], xnor_1_out[3], xnor_1_out[4], xnor_1_out[5], xnor_1_out[6], xnor_1_out[7], xnor_1_out[8], xnor_1_out[9], xnor_1_out[10], xnor_1_out[11], xnor_1_out[12], xnor_1_out[13], xnor_1_out[14], xnor_1_out[15], xnor_1_out[16], xnor_1_out[17], xnor_1_out[18], xnor_1_out[19], xnor_1_out[20], xnor_1_out[21], xnor_1_out[22], xnor_1_out[23]);
endmodule

module test_reg_file (
  input  [31:0] R15,
  input  we,
  input  [3:0] writeAddr,
  input  [31:0] writeData,
  input  clk,
  input  Reset,
  input  [3:0] A1,
  input  [3:0] A2,
  input  [3:0] get_reg_data,
  input  [3:0] get_reg_data_2,
  output [31:0] RD1,
  output [31:0] RD2,
  output [31:0] out_13,
  output [31:0] reg_data
);

  wire decoder_1_out0, decoder_1_out1, decoder_1_out2, decoder_1_out3, decoder_1_out4, decoder_1_out5,
       decoder_1_out6, decoder_1_out7, decoder_1_out8, decoder_1_out9, decoder_1_out10, decoder_1_out11,
       decoder_1_out12, decoder_1_out13, decoder_1_out14;
  wire [31:0] R0_q, R1_q, R2_q, R3_q, R5_q, R6_q, R7_q, R8_q, R9_q, R10_q, R11_q, R12_q, R13_q, R14_q,
       register_1_q;

  Decoder #(.select(4), .disabled(0)) decoder_1 (
    .out0(decoder_1_out0), .out1(decoder_1_out1), .out2(decoder_1_out2), .out3(decoder_1_out3),
    .out4(decoder_1_out4), .out5(decoder_1_out5), .out6(decoder_1_out6), .out7(decoder_1_out7),
    .out8(decoder_1_out8), .out9(decoder_1_out9), .out10(decoder_1_out10), .out11(decoder_1_out11),
    .out12(decoder_1_out12), .out13(decoder_1_out13), .out14(decoder_1_out14), .sel(writeAddr), .en(we));  // open: out15
  Register #(.width(32)) R0 (.D(writeData), .en(decoder_1_out0), .Q(R0_q), .clk(clk), .clr(Reset));
  Register #(.width(32)) R1 (.D(writeData), .en(decoder_1_out1), .Q(R1_q), .clk(clk), .clr(Reset));
  Register #(.width(32)) R2 (.D(writeData), .en(decoder_1_out2), .Q(R2_q), .clk(clk), .clr(Reset));
  Register #(.width(32)) R3 (.D(writeData), .en(decoder_1_out3), .Q(R3_q), .clk(clk), .clr(Reset));
  Register #(.width(32)) register_1 (.D(writeData), .en(decoder_1_out4), .Q(register_1_q), .clk(clk), .clr(Reset));
  Register #(.width(32)) R5 (.D(writeData), .en(decoder_1_out5), .Q(R5_q), .clk(clk), .clr(Reset));
  Register #(.width(32)) R6 (.D(writeData), .en(decoder_1_out6), .Q(R6_q), .clk(clk), .clr(Reset));
  Register #(.width(32)) R7 (.D(writeData), .en(decoder_1_out7), .Q(R7_q), .clk(clk), .clr(Reset));
  Register #(.width(32)) R8 (.D(writeData), .en(decoder_1_out8), .Q(R8_q), .clk(clk), .clr(Reset));
  Register #(.width(32)) R9 (.D(writeData), .en(decoder_1_out9), .Q(R9_q), .clk(clk), .clr(Reset));
  Register #(.width(32)) R10 (.D(writeData), .en(decoder_1_out10), .Q(R10_q), .clk(clk), .clr(Reset));
  Register #(.width(32)) R11 (.D(writeData), .en(decoder_1_out11), .Q(R11_q), .clk(clk), .clr(Reset));
  Register #(.width(32)) R12 (.D(writeData), .en(decoder_1_out12), .Q(R12_q), .clk(clk), .clr(Reset));
  Register #(.width(32)) R13 (.D(writeData), .en(decoder_1_out13), .Q(R13_q), .clk(clk), .clr(Reset));
  Register #(.width(32)) R14 (.D(writeData), .en(decoder_1_out14), .Q(R14_q), .clk(clk), .clr(Reset));
  Multiplexer #(.select(4), .width(32)) multiplexer_1 (
    .in0(R0_q), .in1(R1_q), .in2(R2_q), .in3(R3_q), .in4(register_1_q), .in5(R5_q), .in6(R6_q), .in7(R7_q),
    .in8(R8_q), .in9(R9_q), .in10(R10_q), .in11(R11_q), .in12(R12_q), .in13(R13_q), .in14(R14_q), .in15(R15),
    .out(RD1), .sel(A1));  // open: en
  Multiplexer #(.select(4), .width(32)) multiplexer_2 (
    .in0(R0_q), .in1(R1_q), .in2(R2_q), .in3(R3_q), .in4(register_1_q), .in5(R5_q), .in6(R6_q), .in7(R7_q),
    .in8(R8_q), .in9(R9_q), .in10(R10_q), .in11(R11_q), .in12(R12_q), .in13(R13_q), .in14(R14_q), .in15(R15),
    .out(RD2), .sel(A2));  // open: en
  Multiplexer #(.select(4), .width(32)) multiplexer_3 (
    .in0(R0_q), .in1(R1_q), .in2(R2_q), .in3(R3_q), .in4(register_1_q), .in5(R5_q), .in6(R6_q), .in7(R7_q),
    .in8(R8_q), .in9(R9_q), .in10(R10_q), .in11(R11_q), .in12(R12_q), .in13(R13_q), .in14(R14_q), .in15(R15),
    .out(out_13), .sel(get_reg_data));  // open: en
  Multiplexer #(.select(4), .width(32)) multiplexer_4 (
    .in0(R0_q), .in1(R1_q), .in2(R2_q), .in3(R3_q), .in4(register_1_q), .in5(R5_q), .in6(R6_q), .in7(R7_q),
    .in8(R8_q), .in9(R9_q), .in10(R10_q), .in11(R11_q), .in12(R12_q), .in13(R13_q), .in14(R14_q), .in15(R15),
    .out(reg_data), .sel(get_reg_data_2));  // open: en

  // Notes on the sheet:
  //   A1,A2,-> one of 16 registers as src operands
  //   write port takes 4-bit address input A3; 32-bit write data input WD3; Write enable input WE3; and clock
  //   if the write enable is asserted, reg file writes data into specified reg on rising edge of clock
  //   a read of r15 returns the value from PC + 8 and writes to r15 must be specifically handled to update the pc bc it is separate from reg file
  //   RD1, RD2 -> take A1 and A2
  //   reads 32-bit reg vals of A1, and A2 onto RD1 and RD2
endmodule

module tunnel (
  input  in_1,
  output out_2
);


  assign out_2 = in_1;

  // Other names for the same wires on the sheet: A = in_1
endmodule

module is_bl (
  input  [1:0] Op,
  input  bit24,
  output isBL
);

  wire and_1_out;

  and and_1 (and_1_out, Op[1], ~Op[0]);  // AND_Gate
  and and_2 (isBL, and_1_out, bit24);
endmodule
